// Logisim project Assignment_2.circ as structural Verilog: 1 circuit, main circuit main
module main (
  input  W,
  input  Reset,
  output T3,
  output T2,
  output T1,
  output T0
);

  wire Clock_out, or_1_out, T0_q, T1_q, T2_q, T3_q, T3_qn;

  Clock Clock (.out(Clock_out));
  T_Flip_Flop u_T3 (.clk(Clock_out), .T(T3), .Q(T3_q), .Qn(T3_qn), .reset(Reset), .en(W));  // open: preset
  T_Flip_Flop u_T2 (.clk(Clock_out), .T(T2), .Q(T2_q), .reset(Reset), .en(W));  // open: Qn, preset
  T_Flip_Flop u_T1 (.clk(Clock_out), .T(T1), .Q(T1_q), .reset(Reset), .en(W));  // open: Qn, preset
  T_Flip_Flop u_T0 (.clk(Clock_out), .T(W), .Q(T0_q), .reset(Reset), .en(W));  // open: Qn, preset
  or or_1 (or_1_out, T3_q, T2_q);
  and and_1 (T3, or_1_out, W, T1_q, T0_q);
  and and_2 (T2, T3_qn, T1_q, W, T0_q);
  and and_3 (T1, W, T0_q);

  assign T0 = W;
endmodule
